# Fritzing sketch ledstoplight_circuit (saved by Fritzing 0.9.2b)
breadboards: 1

parts:
  Raspberry_Pi1 = Raspberry Pi 2
  LED1 = LED - 5mm [color="Red (633nm)" package="5 mm [THT]"]
  LED2 = LED - 5mm [color="Green (560nm)" package="5 mm [THT]"]
  R1 = Resistor [tolerance=±5% resistance=220 package=THT]
  R2 = Resistor [tolerance=±5% resistance=220 package=THT]

nets:
  N1: Raspberry_Pi1.GND, R1.Pin_1, R2.Pin_1
  N2: Raspberry_Pi1.GPIO21, LED2.anode
  N3: Raspberry_Pi1.GPIO20, LED1.anode
  N4: LED1.cathode, R1.Pin_0
  N5: LED2.cathode, R2.Pin_0
